// Digital circuit TermProj.dig as structural Verilog
module TermProj (
  input  CLK,
  input  EN,
  input  LOAD,
  input  [3:0] D
);

  wire and_1_out, comparator_1_eq, register_1_q;

  Comparator comparator_1 (.b(register_1_q), .eq(comparator_1_eq));  // open: a, gt, lt
  and and_1 (and_1_out, EN, comparator_1_eq);
  Register register_1 (.D(D[0]), .en(and_1_out), .Q(register_1_q));  // open: C
  Seven_Seg_Hex seven_seg_hex_1 ();  // open: d, dp
  Seven_Seg_Hex seven_seg_hex_2 ();  // open: d, dp
  Seven_Seg_Hex seven_seg_hex_3 ();  // open: d, dp
  Seven_Seg_Hex seven_seg_hex_4 ();  // open: d, dp
  // Pins of 1 and 4 bits meet at D
endmodule
